// Logisim project lab1-2-week5.circ as structural Verilog: 1 circuit, main circuit main
module main (
  input  A,
  input  B,
  input  C,
  input  A_2,
  input  B_2,
  input  C_2,
  output F1,
  output F2
);

  wire and_1_out, and_2_out, and_3_out, and_4_out, and_5_out, and_6_out, nand_1_out, nand_2_out, not_1_out,
       not_2_out, or_1_out, or_2_out, xor_1_out;

  nand nand_1 (nand_1_out, A, B);
  not not_1 (not_1_out, A);
  not not_2 (not_2_out, A_2);
  nand nand_2 (nand_2_out, C_2, B_2);
  or or_1 (or_1_out, nand_1_out, C);
  and and_1 (and_1_out, not_2_out, B_2);
  and and_2 (and_2_out, not_2_out, or_2_out);
  or or_2 (or_2_out, nand_2_out, A_2);
  and and_3 (and_3_out, nand_2_out, C_2);
  and and_4 (and_4_out, C_2, B_2);
  and and_5 (and_5_out, or_1_out, not_1_out);
  and and_6 (and_6_out, not_1_out, C);
  xor xor_1 (xor_1_out, and_3_out, and_4_out);
  xor xor_2 (F1, and_5_out, and_6_out);
  or or_3 (F2, and_1_out, and_2_out, xor_1_out);
endmodule
