// Logisim project lab1-week5.circ as structural Verilog: 1 circuit, main circuit main
module main (
  input  A,
  input  B,
  input  C,
  input  A_2,
  input  B_2,
  input  C_2,
  input  A_3,
  input  B_3,
  input  C_3,
  output F1,
  output F2,
  output F3
);

  wire and_1_out, and_2_out, and_3_out, and_4_out, and_5_out, and_6_out, and_7_out, and_8_out, and_9_out,
       and_10_out, nand_1_out, nor_1_out, not_1_out, not_2_out, not_3_out, not_4_out, not_5_out, not_6_out,
       not_7_out, not_8_out, or_1_out, or_2_out, or_3_out;

  not not_1 (not_1_out, B);
  not not_2 (not_2_out, C_3);
  and and_1 (and_1_out, A, B);
  and and_2 (and_2_out, A, C);
  and and_3 (and_3_out, not_1_out, C);
  and and_4 (and_4_out, A_2, B_2, not_3_out);
  not not_3 (not_3_out, C_2);
  not not_4 (not_4_out, A_2);
  and and_5 (and_5_out, not_4_out, B_2, C_2);
  and and_6 (and_6_out, A_2, not_5_out);
  not not_5 (not_5_out, B_2);
  and and_7 (and_7_out, B_2, not_6_out);
  not not_6 (not_6_out, A_2);
  not not_7 (not_7_out, A_3);
  or or_1 (or_1_out, not_7_out, B_3);
  and and_8 (and_8_out, B_3, not_2_out);
  nand nand_1 (nand_1_out, B_3, C_3);
  not not_8 (not_8_out, and_1_out);
  nor nor_1 (nor_1_out, and_4_out, and_5_out);
  or or_2 (or_2_out, and_6_out, and_7_out);
  and and_9 (and_9_out, or_1_out, or_3_out);
  or or_3 (or_3_out, B_3, and_8_out);
  and and_10 (and_10_out, A_3, nand_1_out);
  or or_4 (F1, not_8_out, and_2_out, and_3_out);
  and and_11 (F2, nor_1_out, or_2_out);
  or or_5 (F3, and_9_out, and_10_out);
endmodule
