// Logisim project Lab3-week7.circ as structural Verilog
module _4_bit_register (
  input  INC,
  input  LD,
  input  [3:0] INPUT,
  input  CLK,
  input  CLR,
  output [3:0] OUTPUT
);

  wire and_1_out, and_2_out, and_3_out, and_4_out, and_5_out, and_6_out, and_7_out, and_8_out, and_9_out,
       and_10_out, and_11_out, and_12_out, not_1_out, not_2_out, not_3_out, not_4_out, not_5_out, or_1_out,
       or_2_out, or_3_out, or_4_out, or_5_out, or_6_out, or_7_out, or_8_out;

  not not_1 (not_1_out, LD);
  not not_2 (not_2_out, INPUT[0]);
  not not_3 (not_3_out, INPUT[1]);
  not not_4 (not_4_out, INPUT[2]);
  not not_5 (not_5_out, INPUT[3]);
  and and_1 (and_1_out, INC, not_1_out);
  and and_2 (and_2_out, LD, INPUT[0]);
  and and_3 (and_3_out, LD, not_2_out);
  and and_4 (and_4_out, LD, INPUT[1]);
  and and_5 (and_5_out, LD, not_3_out);
  and and_6 (and_6_out, LD, INPUT[2]);
  and and_7 (and_7_out, LD, not_4_out);
  and and_8 (and_8_out, LD, INPUT[3]);
  and and_9 (and_9_out, LD, not_5_out);
  or or_1 (or_1_out, and_2_out, and_1_out);
  or or_2 (or_2_out, and_3_out, and_1_out);
  or or_3 (or_3_out, and_4_out, and_10_out);
  and and_10 (and_10_out, and_1_out, OUTPUT[0]);
  or or_4 (or_4_out, and_10_out, and_5_out);
  or or_5 (or_5_out, and_6_out, and_11_out);
  and and_11 (and_11_out, and_1_out, OUTPUT[0], OUTPUT[1]);
  or or_6 (or_6_out, and_11_out, and_7_out);
  or or_7 (or_7_out, and_8_out, and_12_out);
  and and_12 (and_12_out, and_1_out, OUTPUT[0], OUTPUT[1], OUTPUT[2]);
  or or_8 (or_8_out, and_12_out, and_9_out);
  J_K_Flip_Flop j_k_ff_1 (.J(or_1_out), .clk(CLK), .K(or_2_out), .Q(OUTPUT[0]), .reset(CLR));  // open: Qn, preset, en
  J_K_Flip_Flop j_k_ff_2 (.J(or_3_out), .clk(CLK), .K(or_4_out), .Q(OUTPUT[1]), .reset(CLR));  // open: Qn, preset, en
  J_K_Flip_Flop j_k_ff_3 (.J(or_5_out), .clk(CLK), .K(or_6_out), .Q(OUTPUT[2]), .reset(CLR));  // open: Qn, preset, en
  J_K_Flip_Flop j_k_ff_4 (.J(or_7_out), .clk(CLK), .K(or_8_out), .Q(OUTPUT[3]), .reset(CLR));  // open: Qn, preset, en
endmodule
