// Logisim project project.circ as structural Verilog
module _4_bit_register (
  input  INC,
  input  LD,
  input  [3:0] INPUT,
  input  CLK,
  input  CLR,
  output [3:0] OUTPUT
);

  wire and_1_out, and_2_out, and_3_out, and_4_out, and_5_out, and_6_out, and_7_out, and_8_out, and_9_out,
       and_10_out, and_11_out, and_12_out, not_1_out, not_2_out, not_3_out, not_4_out, not_5_out, or_1_out,
       or_2_out, or_3_out, or_4_out, or_5_out, or_6_out, or_7_out, or_8_out;

  not not_1 (not_1_out, LD);
  not not_2 (not_2_out, INPUT[0]);
  not not_3 (not_3_out, INPUT[1]);
  not not_4 (not_4_out, INPUT[2]);
  not not_5 (not_5_out, INPUT[3]);
  and and_1 (and_1_out, INC, not_1_out);
  and and_2 (and_2_out, LD, INPUT[0]);
  and and_3 (and_3_out, LD, not_2_out);
  and and_4 (and_4_out, LD, INPUT[1]);
  and and_5 (and_5_out, LD, not_3_out);
  and and_6 (and_6_out, LD, INPUT[2]);
  and and_7 (and_7_out, LD, not_4_out);
  and and_8 (and_8_out, LD, INPUT[3]);
  and and_9 (and_9_out, LD, not_5_out);
  or or_1 (or_1_out, and_2_out, and_1_out);
  or or_2 (or_2_out, and_3_out, and_1_out);
  or or_3 (or_3_out, and_4_out, and_10_out);
  and and_10 (and_10_out, and_1_out, OUTPUT[0]);
  or or_4 (or_4_out, and_10_out, and_5_out);
  or or_5 (or_5_out, and_6_out, and_11_out);
  and and_11 (and_11_out, and_1_out, OUTPUT[0], OUTPUT[1]);
  or or_6 (or_6_out, and_11_out, and_7_out);
  or or_7 (or_7_out, and_8_out, and_12_out);
  and and_12 (and_12_out, and_1_out, OUTPUT[0], OUTPUT[1], OUTPUT[2]);
  or or_8 (or_8_out, and_12_out, and_9_out);
  J_K_Flip_Flop j_k_ff_1 (.J(or_1_out), .clk(CLK), .K(or_2_out), .Q(OUTPUT[0]), .reset(CLR));  // open: Qn, preset, en
  J_K_Flip_Flop j_k_ff_2 (.J(or_3_out), .clk(CLK), .K(or_4_out), .Q(OUTPUT[1]), .reset(CLR));  // open: Qn, preset, en
  J_K_Flip_Flop j_k_ff_3 (.J(or_5_out), .clk(CLK), .K(or_6_out), .Q(OUTPUT[2]), .reset(CLR));  // open: Qn, preset, en
  J_K_Flip_Flop j_k_ff_4 (.J(or_7_out), .clk(CLK), .K(or_8_out), .Q(OUTPUT[3]), .reset(CLR));  // open: Qn, preset, en
endmodule

module _1_bit_ALU (
  input  INPR,
  input  DR,
  input  AC,
  input  AND,
  input  ADD,
  input  Cin,
  input  CMA,
  input  LD_DR,
  input  LD_NPR,
  input  CIR,
  input  CIL,
  input  AC_i_1,
  input  AC_i_1_2,
  output Cout,
  output output_AC
);

  wire add_out, adder_1_out, and_out, comp_out, ld_DR_out, ld_NPR_out, not_1_out, shl_out, shr_out;

  Adder #(.width(1)) adder_1 (.a(AC), .b(DR), .out(adder_1_out), .cin(Cin), .cout(Cout));
  not not_1 (not_1_out, AC);
  and u_and (and_out, AND, AC, DR);
  and u_add (add_out, ADD, adder_1_out);
  and comp (comp_out, CMA, not_1_out);
  and u_ld_DR (ld_DR_out, LD_DR, DR);
  and u_ld_NPR (ld_NPR_out, LD_NPR, INPR);
  and shr (shr_out, CIR, AC_i_1_2);
  and shl (shl_out, CIL, AC_i_1);
  or or_1 (output_AC, and_out, add_out, comp_out, ld_DR_out, ld_NPR_out, shr_out, shl_out);
endmodule

module _4_bit_ALU (
  input  cin,
  input  E_AC_0,
  input  [3:0] AC,
  input  [3:0] DR,
  input  [3:0] INPR,
  input  AND,
  input  ADD,
  input  CMA,
  input  LD_DR,
  input  LD_NPR,
  input  CIR,
  input  CIL,
  input  E_AC_3,
  output [3:0] output_AC,
  output cout
);

  wire n1_bit_alu_1_cout, n1_bit_alu_2_cout, n1_bit_alu_3_cout;

  _1_bit_ALU u_1_bit_alu_1 (
    .AND(AND), .ADD(ADD), .CMA(CMA), .LD_DR(LD_DR), .LD_NPR(LD_NPR), .CIR(CIR), .CIL(CIL), .AC_i_1(E_AC_0),
    .AC_i_1_2(AC[1]), .INPR(INPR[0]), .DR(DR[0]), .AC(AC[0]), .Cin(cin), .Cout(n1_bit_alu_1_cout),
    .output_AC(output_AC[0]));
  _1_bit_ALU u_1_bit_alu_2 (
    .AND(AND), .ADD(ADD), .CMA(CMA), .LD_DR(LD_DR), .LD_NPR(LD_NPR), .CIR(CIR), .CIL(CIL), .AC_i_1(AC[0]),
    .AC_i_1_2(AC[2]), .INPR(INPR[1]), .DR(DR[1]), .AC(AC[1]), .Cin(n1_bit_alu_1_cout),
    .Cout(n1_bit_alu_2_cout), .output_AC(output_AC[1]));
  _1_bit_ALU u_1_bit_alu_3 (
    .AND(AND), .ADD(ADD), .CMA(CMA), .LD_DR(LD_DR), .LD_NPR(LD_NPR), .CIR(CIR), .CIL(CIL), .AC_i_1(AC[1]),
    .AC_i_1_2(AC[3]), .INPR(INPR[2]), .DR(DR[2]), .AC(AC[2]), .Cin(n1_bit_alu_2_cout),
    .Cout(n1_bit_alu_3_cout), .output_AC(output_AC[2]));
  _1_bit_ALU u_1_bit_alu_4 (
    .AND(AND), .ADD(ADD), .CMA(CMA), .LD_DR(LD_DR), .LD_NPR(LD_NPR), .CIR(CIR), .CIL(CIL), .AC_i_1(AC[2]),
    .AC_i_1_2(E_AC_3), .INPR(INPR[3]), .DR(DR[3]), .AC(AC[3]), .Cin(n1_bit_alu_3_cout), .Cout(cout),
    .output_AC(output_AC[3]));
endmodule

module PC (
  input  T0,
  input  T1,
  input  T3,
  input  T4,
  input  D4,
  input  D5,
  input  D6,
  output PC_LD,
  output PC_INC,
  output PC_BUS
);

  wire and_1_out, and_2_out, and_3_out, or_1_out;

  or or_1 (or_1_out, D6, D4);
  and and_1 (and_1_out, or_1_out, T3);
  and and_2 (and_2_out, D5, T4);
  and and_3 (and_3_out, D5, T3);
  or or_2 (PC_LD, and_1_out, and_2_out);
  or or_3 (PC_BUS, and_3_out, T0);

  assign PC_INC = T1;
endmodule
